# Fritzing sketch SchaltplanMatrix (saved by Fritzing 0.9.3b)

parts:
  NEOPIXEL1 = Neopixel Strip -- Black (30/m)
  Bauteil1 = Arduino Uno (Rev3)
  NEOPIXEL2 = Neopixel Strip -- Black (30/m)
  NEOPIXEL4 = Neopixel Strip -- Black (30/m)  # not connected
  NEOPIXEL5 = Neopixel Strip -- Black (30/m)  # not connected
  Power_plug1 = Power plug
  R1 = Resistor [tolerance=±5% resistance=220 package="2512 [SMD]"]
  C3 = Electrolytic Capacitor [capacitance=1µF package="100 mil [THT, electrolytic]"]

nets:
  GND: NEOPIXEL1.GND#1, Bauteil1.GND, Power_plug1.GND, C3.-
  N1: NEOPIXEL1.Din, R1.Pin_1
  +5V: NEOPIXEL1.+5V, Bauteil1.5V, Power_plug1.VCC, C3.+
  N2: NEOPIXEL1.Dout, NEOPIXEL2.Din
  N3: Bauteil1.D5_PWM, R1.Pin_0

custom parts:
  Neopixel Strip -- Black (30/m): These NeoPixel strips have 30 digitally-addressable pixel LEDs per meter and are very affordable and are only 12.5 mm wide, 10 mm if you remove the strip from the casing.
